# Fritzing sketch VitoWifi (saved by Fritzing 0.9.1b)
circuit board: 4.766cm x 4.03607cm

parts:
  U1 = ESP8266 WiFi Module [part_number=ESP8266]
  LED1 = LED - 3mm [color="Red (633nm)" package="3 mm [THT]"]
  to_OTGW = female pin header, 3 pins [form="♀ (female)"]
  Sensors = female pin header, 3 pins [form="♀ (female)"]
  GND_3V3 = Screw terminal - 2 pins [package=THT]
  R4 = Resistor [tolerance=±5% resistance=1k package=THT]
  R3 = Resistor [tolerance=±5% resistance=2.2k package=THT]
  R1 = Resistor [tolerance=±5% resistance=4.7k package=THT]
  R2 = Resistor [tolerance=±5% resistance=220 package=THT]

nets:
  N1: U1.RXD, R4.Pin_1, R3.Pin_0
  N2: U1.VCC, U1.CH_PD, Sensors.pin3, GND_3V3.pin1, R1.Pin_0, R2.Pin_0
  N3: U1.GPIO_0, LED1.cathode
  N4: U1.GPIO_2, Sensors.pin2, R1.Pin_1
  N5: U1.GND, to_OTGW.pin2, Sensors.pin1, GND_3V3.pin2, R3.Pin_1
  N6: U1.TXD, to_OTGW.pin1
  N7: LED1.anode, R2.Pin_1
  N8: to_OTGW.pin3, R4.Pin_0

notes:
  -> TX
  -> GND
  -> RX
  3.3V
  GND
  VCC
  Data
  GND

custom parts:
  ESP8266 WiFi Module: Generic WiFi Module based on the ESP8266 with onboard PCB antenna and UART communications
